# Fritzing sketch DHTSchem (saved by Fritzing 0.9.3b)
breadboards: 1

parts:
  RHT1 = Humidity and Temperature Sensor RHT03
  Part1 = Arduino Nano (Rev3.0)
  R1 = Resistor [tolerance=±5% resistance=10k package="1206 [SMD]"]

nets:
  VCC: RHT1.Vcc, Part1.5V
  N1: RHT1.Data-signal, Part1.D13/SCK, R1.Pin_0
  N2: RHT1.GND_2, Part1.GND
