# Fritzing sketch lcdschem (saved by Fritzing 0.9.3b)
breadboards: 1

parts:
  Part1 = Arduino Nano (Rev3.0) (ICSP)
  U1 = LCD-16X2 [package=lcd-16x2_noholes]

nets:
  N1: Part1.GND, U1.DB5
  N2: Part1.5V, U1.DB6
  N3: Part1.A5, U1.DB2
  N4: Part1.A4, U1.DB3
